# Fritzing sketch Placa (saved by Fritzing 0.9.3b)

parts:
  U1 = ESP32-WROOM-32D-NodeMCU
  M1 = Getriebemotor
  M2 = Getriebemotor
  L298N1 = L298N DC motor driver
  HC-SR04_Sensor_1 = HC-SR04 Ultrasonic Distance Sensor
  VCC1 = Battery
  HC-SR04_Sensor_2 = HC-SR04 Ultrasonic Distance Sensor  # not connected
  ESP32_-_Front1 = ESP32 - CAM  # not connected
  J1 = Basic Servo  # not connected

nets:
  N1: U1.G26, L298N1.IN1
  N2: U1.G27, L298N1.IN2
  N3: U1.G14, L298N1.IN3
  N4: U1.G12, L298N1.IN4
  5V: U1.5V, L298N1.5V, HC-SR04_Sensor_1.VCC
  N5: U1.G15, L298N1.ENB
  N6: U1.G2, L298N1.ENA
  N7: U1.G5, HC-SR04_Sensor_1.TRIG
  N8: U1.G18, HC-SR04_Sensor_1.ECHO
  GND: U1.GND, L298N1.GND, HC-SR04_Sensor_1.GND, VCC1.-
  N9: M1.pin_1, L298N1.OUT1
  N10: M2.pin_1, L298N1.OUT3

custom parts:
  L298N DC motor driver: 2x DC motor driver with 78M05 positive voltage regulator (7..35 V) L298N: max 46 V, 2 A Set 5 V Enable jumper to enable 5 V regultor (needed for the L298N) and +5 V output at screw terminal or supply external +5 V at screw terminal Set ENA and/or ENB to +5 V to enable motor permanently or supply ENA and/or ENB with PWM signal IN1 and IN2 set rotation directory for motor A (OUT1/OUT2) IN2 and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
  Battery: Your standard 2x 18650 battery pack (7,4 Volts)
  ESP32 - CAM: The ESP32-CAM has a very competitive small-size camera module that can operate independently as a minimum system with a footprint of only 27*40.5*4.5mm and a deep sleep current of up to 6mA.
